# Fritzing sketch 8Ohm_Speaker_Arduino (saved by Fritzing 0.8.7b)
breadboards: 1

parts:
  Arduino1 = Arduino Uno (Rev3)
  SPKR1 = Loudspeaker
  R1 = Resistor [tolerance=±5% resistance=100 package=THT]

nets:
  N1: Arduino1.GND, SPKR1.pin1
  N2: Arduino1.D3_PWM, R1.Pin_1
  N3: SPKR1.pin2, R1.Pin_0
