# Fritzing sketch AnalogHigherLoad (saved by Fritzing 0.8.7b)
breadboards: 1

parts:
  Q1 = MOSFET-NCHANNEL [package=to220v]
  D1 = Rectifier Diode [part_number=1N4001 package="300 mil [THT]"]
  Part1 = Arduino Uno (Rev3)
  C1 = Electrolytic Capacitor [capacitance=10µF package="100 mil [THT, electrolytic]"]
  M1 = DC Motor
  VCC1 = Battery block 9V
  R1 = Resistor [tolerance=±5% resistance=10k package=THT]

nets:
  N1: Q1.G, Part1.D3_PWM, R1.Pin_0
  N2: Q1.D, D1.anode, M1.pin_2
  GND: Q1.S, Part1.GND, C1.-, VCC1.-, R1.Pin_1
  12V/9V: D1.cathode, Part1.VIN, C1.+, M1.pin_1, VCC1.+
