# Fritzing sketch Analog_Pot_And_LED (saved by Fritzing 0.8.7b)
breadboards: 1

parts:
  Arduino1 = Arduino Uno (Rev3)
  LED1 = LED - 5mm [color="Red (633nm)" package="5 mm [THT]"]
  R1 = Resistor [tolerance=±5% resistance=330 package=THT]
  R2 = Rotary Potentiometer (Small) [maximum_resistance=10kΩ package=THT]

nets:
  N1: Arduino1.A0, R2.wiper
  N2: Arduino1.D3_PWM, LED1.anode
  N3: Arduino1.5V, R2.leg1
  N4: Arduino1.GND, R1.Pin_0, R2.leg2
  N5: LED1.cathode, R1.Pin_1
