# Fritzing sketch External_LED_Arduino_Source (saved by Fritzing 0.8.7b)
breadboards: 1

parts:
  Arduino1 = Arduino Uno (Rev3)
  LED1 = LED - 5mm [color="Red (633nm)" package="5 mm [THT]"]
  R1 = Resistor [tolerance=±5% resistance=330 package=THT]

nets:
  N1: Arduino1.D3_PWM, LED1.anode
  N2: Arduino1.GND, R1.Pin_0
  N3: LED1.cathode, R1.Pin_1
