# Fritzing sketch RGB_LED_3Pots_Arduino (saved by Fritzing 0.8.7b)
breadboards: 1

parts:
  Arduino1 = Arduino Uno (Rev3)
  R1 = Resistor [tolerance=±5% resistance=220 package=THT]
  R2 = Resistor [tolerance=±5% resistance=180 package=THT]
  R3 = Resistor [tolerance=±5% resistance=180 package=THT]
  LED1 = RGB LED - (4 legs) [package="5 mm [THT]"]
  R4 = TRIMPOT [package=trimpot_pth_s3_lock]
  R5 = TRIMPOT [package=trimpot_pth_s3_lock]
  R6 = TRIMPOT [package=trimpot_pth_s3_lock]

nets:
  N1: Arduino1.A0, R4.WIPER
  N2: Arduino1.A1, R5.WIPER
  N3: Arduino1.A2, R6.WIPER
  N4: Arduino1.D3_PWM, R1.Pin_0
  N5: Arduino1.D5_PWM, R2.Pin_0
  N6: Arduino1.D6_PWM, R3.Pin_0
  N7: Arduino1.5V, LED1.common_anode, R4.CCW, R5.CCW, R6.CCW
  GND: Arduino1.GND, R4.CW, R5.CW, R6.CW
  N8: R1.Pin_1, LED1.red_cathode
  N9: R2.Pin_1, LED1.green_cathode
  N10: R3.Pin_1, LED1.blue_cathode
