# Fritzing sketch RGB_LED_Arduino_Sink (saved by Fritzing 0.8.7b)
breadboards: 1

parts:
  Arduino1 = Arduino Uno (Rev3)
  R1 = Resistor [tolerance=±5% resistance=220 package=THT]
  R2 = Resistor [tolerance=±5% resistance=180 package=THT]
  R3 = Resistor [tolerance=±5% resistance=180 package=THT]
  LED1 = RGB LED - (4 legs) [package="5 mm [THT]"]

nets:
  N1: Arduino1.D3_PWM, R1.Pin_0
  N2: Arduino1.D5_PWM, R2.Pin_0
  N3: Arduino1.D6_PWM, R3.Pin_0
  N4: Arduino1.5V, LED1.common_anode
  N5: R1.Pin_1, LED1.red_cathode
  N6: R2.Pin_1, LED1.green_cathode
  N7: R3.Pin_1, LED1.blue_cathode
