# Fritzing sketch RGB_LED_Arduino_Source (saved by Fritzing 0.8.7b)
breadboards: 1

parts:
  Arduino1 = Arduino Uno (Rev3)
  LED1 = RGB LED (com. cathode, rbg) [package="5 mm [THT]"]
  R1 = Resistor [tolerance=±5% resistance=220 package=THT]
  R2 = Resistor [tolerance=±5% resistance=180 package=THT]
  R3 = Resistor [tolerance=±5% resistance=180 package=THT]

nets:
  N1: Arduino1.D3_PWM, R1.Pin_0
  N2: Arduino1.D5_PWM, R2.Pin_0
  N3: Arduino1.D6_PWM, R3.Pin_0
  N4: Arduino1.GND, LED1.common_cathode
  N5: LED1.red_anode, R1.Pin_1
  N6: LED1.blue_anode, R2.Pin_1
  N7: LED1.green_anode, R3.Pin_1
