# Fritzing sketch RGB_Strip_3Pots_Arduino (saved by Fritzing 0.8.7b)
breadboards: 1

parts:
  Arduino1 = Arduino Uno (Rev3)
  LED1 = RGB LED - (4 legs) [package="5 mm [THT]"]
  Q2 = Basic FET N-Channel [package="TO220 [THT]"]
  Q3 = Basic FET N-Channel [package="TO220 [THT]"]
  Q4 = Basic FET N-Channel [package="TO220 [THT]"]
  R1 = Resistor [tolerance=±5% resistance=10k package=THT]
  R2 = Resistor [tolerance=±5% resistance=10k package=THT]
  R3 = Resistor [tolerance=±5% resistance=10k package=THT]
  R6 = TRIMPOT [package=trimpot_pth_s3_lock]
  R8 = TRIMPOT [package=trimpot_pth_s3_lock]
  R7 = TRIMPOT [package=trimpot_pth_s3_lock]

nets:
  N1: Arduino1.A0, R6.WIPER
  N2: Arduino1.A1, R7.WIPER
  N3: Arduino1.A2, R8.WIPER
  N4: Arduino1.D3_PWM, Q3.gate, R3.Pin_1
  N5: Arduino1.D5_PWM, Q2.gate, R2.Pin_1
  N6: Arduino1.D6_PWM, Q4.gate, R1.Pin_1
  N7: Arduino1.5V, R6.CCW, R8.CCW, R7.CCW
  GND: Arduino1.GND, Q2.source, Q3.source, Q4.source, R1.Pin_0, R2.Pin_0, R3.Pin_0, R6.CW, R8.CW, R7.CW
  12V: Arduino1.VIN, LED1.common_anode
  N8: LED1.red_cathode, Q3.drain
  N9: LED1.green_cathode, Q2.drain
  N10: LED1.blue_cathode, Q4.drain
