# Fritzing sketch ICE_X (saved by Fritzing 0.7.12b)
breadboards: 1

parts:
  Q1 = NPN-Transistor [package="TO92 [THT]"]
  R1 = Resistor [tolerance=±5% resistance=220 package=THT]
  S1 = Pushbutton [package=THT]
  LED1 = LED - 5mm [color="Red (633nm)" package="5 mm [THT]"]
  R2 = Resistor [tolerance=±5% resistance=220 package=THT]

nets:
  GND: Q1.E
  N1: Q1.B, R1.Pin_1
  N2: Q1.C, LED1.cathode
  N3: R1.Pin_0, S1.leg0
  5V: S1.leg1, R2.Pin_0
  N4: LED1.anode, R2.Pin_1
