# Fritzing sketch ICE_XI (saved by Fritzing 0.7.12b)
breadboards: 1

parts:
  Q1 = NPN-Transistor [package="TO92 [THT]"]
  M1 = DC Motor
  C1 = Electrolytic Capacitor [capacitance=1µF package="100 mil [THT, electrolytic]"]
  D1 = Rectifier Diode [part_number=1N4001 package="300 mil [THT]"]
  R1 = Resistor [tolerance=±5% resistance=220 package=THT]
  S1 = Pushbutton [package=THT]

nets:
  GND: Q1.E, C1.-
  N1: Q1.B, R1.Pin_1
  N2: Q1.C, M1.pin_1, D1.anode
  9V: M1.pin_2, C1.+, D1.cathode
  N3: R1.Pin_0, S1.leg0
  5V: S1.leg1
