# Fritzing sketch InClassExcercise_IANDII (saved by Fritzing 0.7.12b)
breadboards: 1

parts:
  R1 = Resistor [tolerance=±5% resistance=220 package=THT]
  R2 = Resistor [tolerance=±5% resistance=220 package=THT]
  R3 = Resistor [tolerance=±5% resistance=220 package=THT]
  Fuse1 = Fuse with Handler [part_number=Solder]

nets:
  N1: R1.Pin_0, Fuse1.Connector2
  N2: R1.Pin_1, R2.Pin_0
  N3: R2.Pin_1, R3.Pin_0
  GND: R3.Pin_1
  12V: Fuse1.Connector1
