# Fritzing sketch InClassExcercise_IV (saved by Fritzing 0.7.12b)
breadboards: 1

parts:
  Fuse1 = Fuse with Handler [part_number=Solder]
  LED1 = LED - 5mm [color="Red (633nm)" package="5 mm [THT]"]
  R1 = Resistor [tolerance=±5% resistance=220 package=THT]
  J1 = Basic Force Sensing Resistor (FSR) [package=THT]

nets:
  5V: Fuse1.Connector1
  N1: Fuse1.Connector2, R1.Pin_0
  GND: LED1.cathode
  N2: LED1.anode, J1.pin_1
  N3: R1.Pin_1, J1.pin_0
