# Fritzing sketch InClassExcercise_IV_old (saved by Fritzing 0.7.12b)
breadboards: 1

parts:
  R1 = Resistor [tolerance=±5% resistance=220 package=THT]
  Fuse1 = Fuse with Handler [part_number=Solder]
  Fuse2 = Fuse with Handler [part_number=Solder]
  J1 = Basic Force Sensing Resistor (FSR) [package=THT]
  R2 = Resistor [tolerance=±5% resistance=220 package=THT]
  LED1 = LED - 5mm [color="Red (633nm)" package="5 mm [THT]"]

nets:
  N1: R1.Pin_0, Fuse1.Connector2
  N2: R1.Pin_1, LED1.anode
  12V: Fuse1.Connector1, Fuse2.Connector1
  N3: Fuse2.Connector2, J1.pin_0
  N4: J1.pin_1, R2.Pin_0
  GND: R2.Pin_1, LED1.cathode
