# Fritzing sketch InClassExcercise_VIII (saved by Fritzing 0.7.12b)
breadboards: 1

parts:
  J1 = Basic Force Sensing Resistor (FSR) [package=THT]
  S1 = Pushbutton [package=THT]
  M1 = DC Motor

nets:
  N1: J1.pin_0, S1.leg0
  N2: J1.pin_1, M1.pin_1
  5V: S1.leg1
  GND: M1.pin_2
