# Fritzing sketch InclassExample_1 (saved by Fritzing 0.7.12b)
breadboards: 1

parts:
  M1 = DC Motor
  C1 = Electrolytic Capacitor [capacitance=1µF package="100 mil [THT, electrolytic]"]
  D1 = Rectifier Diode [part_number=1N4001 package="300 mil [THT]"]
  Arduino1 = Arduino  # not connected

nets:
  N1: M1.pin_1, C1.+, D1.cathode
  N2: M1.pin_2, D1.anode
